// Logisim project IT012_Lab02_25521844.circ as structural Verilog: 8 circuits, main circuit FA
module FA (
  input  A,
  input  B,
  input  Cin,
  output Cout,
  output S
);

  wire and_1_out, and_2_out, xor_1_out;

  xor xor_1 (xor_1_out, A, B);
  and and_1 (and_1_out, A, B);
  xor xor_2 (S, xor_1_out, Cin);
  and and_2 (and_2_out, Cin, xor_1_out);
  or or_1 (Cout, and_1_out, and_2_out);
endmodule

module ADDSUB4 (
  input  [3:0] A,
  input  [3:0] B,
  input  SUB,
  output [3:0] S,
  output C
);

  wire fa_1_cout, fa_2_cout, fa_3_cout, xor_1_out, xor_2_out, xor_3_out, xor_4_out;

  // Probe on fa_3_cout
  FA fa_1 (.A(A[0]), .B(xor_1_out), .Cin(SUB), .Cout(fa_1_cout), .S(S[0]));
  FA fa_2 (.A(A[2]), .B(xor_3_out), .Cin(fa_3_cout), .Cout(fa_2_cout), .S(S[2]));
  xor xor_1 (xor_1_out, B[0], SUB);
  FA fa_3 (.A(A[1]), .B(xor_2_out), .Cin(fa_1_cout), .Cout(fa_3_cout), .S(S[1]));
  // Probe on fa_1_cout
  // Probe on fa_2_cout
  FA fa_4 (.A(A[3]), .B(xor_4_out), .Cin(fa_2_cout), .Cout(C), .S(S[3]));
  xor xor_2 (xor_2_out, B[1], SUB);
  xor xor_3 (xor_3_out, B[2], SUB);
  xor xor_4 (xor_4_out, B[3], SUB);
endmodule

module ALU8 (
  input  [7:0] A,
  input  [7:0] B,
  input  [2:0] OP,
  output [7:0] R,
  output Z,
  output LT
);

  wire and_2_out, and_3_out, and_4_out, not_2_out;
  wire [7:0] adder_1_out, adder_2_out, and_1_out, multiplexer_1_out, multiplexer_2_out, not_1_out, or_1_out,
       subtractor_1_out, subtractor_2_out, xor_1_out;

  Adder adder_1 (.a(A), .b(B), .out(adder_1_out));  // open: cin, cout
  Adder adder_2 (.a(A), .b(8'h1), .out(adder_2_out));  // open: cin, cout
  Subtractor subtractor_1 (.a(A), .b(B), .out(subtractor_1_out));  // open: bin, bout
  Subtractor subtractor_2 (.a(A), .b(8'h1), .out(subtractor_2_out));  // open: bin, bout
  assign and_1_out = A & B;  // AND_Gate and_1, 8 bits wide
  assign or_1_out = A | B;  // OR_Gate or_1, 8 bits wide
  assign not_1_out = ~A;  // NOT_Gate not_1, 8 bits wide
  assign xor_1_out = A ^ B;  // XOR_Gate xor_1, 8 bits wide
  not not_2 (not_2_out, B[7]);
  Multiplexer #(.select(2), .width(8)) multiplexer_1 (
    .in0(adder_1_out), .in1(adder_2_out), .in2(subtractor_1_out), .in3(subtractor_2_out),
    .out(multiplexer_1_out), .sel(OP[1:0]));
  Multiplexer #(.select(2), .width(8)) multiplexer_2 (
    .in0(and_1_out), .in1(or_1_out), .in2(not_1_out), .in3(xor_1_out), .out(multiplexer_2_out), .sel(OP[1:0]));
  and and_2 (and_2_out, A[7], R[7]);
  and and_3 (and_3_out, A[7], not_2_out);
  Multiplexer #(.width(8)) multiplexer_3 (.in0(multiplexer_1_out), .in1(multiplexer_2_out), .out(R), .sel(OP[2]));
  or or_2 (LT, and_2_out, and_3_out, and_4_out);
  and and_4 (and_4_out, R[7], not_2_out);
  nor nor_1 (Z, R[0], R[1], R[2], R[3], R[4], R[5], R[7]);
endmodule

module DLATCH (
  input  D,
  input  E,
  output out_3
);

  Multiplexer multiplexer_1 (.in0(out_3), .in1(D), .out(out_3), .sel(E));
endmodule

module TN3 (
  input  D,
  input  CLK,
  output Q1,
  output out_4,
  output Q2,
  output out_6,
  output Q3
);

  D_Flip_Flop d_ff_1 (.D(D), .clk(CLK), .Q(Q2));  // open: Qn, preset, reset
  D_Flip_Flop d_ff_2 (.D(Q2), .clk(CLK), .Q(out_6));  // open: Qn, preset, reset
  DLATCH dlatch_1 (.D(D), .E(CLK), .out_3(Q1));
  DFF_MS dff_ms_1 (.D(D), .CLK(CLK), .Q3(Q3));
  DLATCH dlatch_2 (.D(Q1), .E(CLK), .out_3(out_4));
endmodule

module DFF_MS (
  input  D,
  input  CLK,
  output Q3
);

  wire dlatch_1_out_3, not_1_out;

  not not_1 (not_1_out, CLK);
  DLATCH dlatch_1 (.D(D), .E(not_1_out), .out_3(dlatch_1_out_3));
  DLATCH dlatch_2 (.D(dlatch_1_out_3), .E(CLK), .out_3(Q3));
endmodule

module REGFILE (
  input  [1:0] RB,
  input  [1:0] RA,
  input  [7:0] DIN,
  input  CLK,
  input  [1:0] RD,
  input  WE,
  output [7:0] R0,
  output [7:0] QB,
  output [7:0] R1,
  output [7:0] R2,
  output [7:0] R3,
  output [7:0] QA
);

  wire and_1_out, and_2_out, and_3_out, and_4_out, decoder_1_out0, decoder_1_out1, decoder_1_out2,
       decoder_1_out3;

  Decoder #(.enable("false"), .select(2)) decoder_1 (
    .out0(decoder_1_out0), .out1(decoder_1_out1), .out2(decoder_1_out2), .out3(decoder_1_out3), .sel(RD));
  Register register_1 (.D(DIN), .clk(CLK), .Q(R0), .clr(and_1_out));  // open: en
  and and_1 (and_1_out, decoder_1_out0, WE);
  and and_2 (and_2_out, WE, decoder_1_out1);
  and and_3 (and_3_out, decoder_1_out2, WE);
  and and_4 (and_4_out, WE, decoder_1_out3);
  Register register_2 (.D(DIN), .clk(CLK), .Q(R1), .clr(and_2_out));  // open: en
  Register register_3 (.D(DIN), .clk(CLK), .Q(R2), .clr(and_3_out));  // open: en
  Register register_4 (.D(DIN), .clk(CLK), .Q(R3), .clr(and_4_out));  // open: en
  Multiplexer #(.select(2), .width(8)) multiplexer_1 (.in0(R0), .in1(R1), .in2(R2), .in3(R3), .out(QB), .sel(RB));
  Multiplexer #(.select(2), .width(8)) multiplexer_2 (.in0(R0), .in1(R1), .in2(R2), .in3(R3), .out(QA), .sel(RA));
endmodule

module DATAPATH (
  input  [1:0] RB,
  input  [1:0] RA,
  input  CLK,
  input  [1:0] RD,
  input  WE,
  input  [2:0] OP,
  input  [7:0] IMM,
  input  SRC,
  output [7:0] R0,
  output [7:0] R1,
  output [7:0] R2,
  output [7:0] R3,
  output Z,
  output [7:0] R
);

  wire [7:0] multiplexer_1_out, regfile_1_qa, regfile_1_qb;

  REGFILE regfile_1 (
    .RB(RB), .RA(RA), .DIN(multiplexer_1_out), .CLK(CLK), .RD(RD), .WE(WE), .R0(R0), .QB(regfile_1_qb),
    .R1(R1), .R2(R2), .R3(R3), .QA(regfile_1_qa));
  Multiplexer #(.width(8)) multiplexer_1 (.in0(R), .in1(IMM), .out(multiplexer_1_out), .sel(SRC));
  ALU8 alu8_1 (.A(regfile_1_qa), .B(regfile_1_qb), .OP(OP), .R(R), .Z(Z));  // open: LT
endmodule
